# Fritzing sketch az-1-2 (saved by Fritzing 1.0.5)
breadboards: 1

parts:
  R1 = Resistor [tolerance=±5% power=0.25W resistance=220 package=THT]
  LED1 = LED - 5mm [color="Red (633nm)" current=0.030A package="5 mm [THT]"]
  VCC1 = Battery [internal_resistance=0.1Ω]

nets:
  N1: R1.Pin_0, LED1.anode
  N2: R1.Pin_1, VCC1.+
  N3: LED1.cathode, VCC1.-
