// Logisim project bothwayShift.circ as structural Verilog: 1 circuit, main circuit main
module main (
  input  D,
  input  C,
  input  B,
  input  A,
  input  MODE,
  input  S_in
);

  wire and_1_out, and_2_out, and_3_out, and_4_out, and_5_out, and_6_out, and_7_out, and_8_out, button_1_out,
       d_ff_1_q, d_ff_2_q, d_ff_3_q, d_ff_4_q, not_1_out, or_1_out, or_2_out, or_3_out, or_4_out;

  not not_1 (not_1_out, MODE);
  and and_1 (and_1_out, S_in, MODE);
  and and_2 (and_2_out, not_1_out, d_ff_2_q);
  and and_3 (and_3_out, d_ff_1_q, MODE);
  and and_4 (and_4_out, not_1_out, d_ff_3_q);
  buf and_5 (and_5_out, d_ff_2_q);  // AND_Gate
  and and_6 (and_6_out, not_1_out, d_ff_4_q);
  and and_7 (and_7_out, d_ff_3_q, MODE);
  and and_8 (and_8_out, not_1_out, S_in);
  or or_1 (or_1_out, and_1_out, and_2_out);
  or or_2 (or_2_out, and_3_out, and_4_out);
  or or_3 (or_3_out, and_5_out, and_6_out);
  or or_4 (or_4_out, and_7_out, and_8_out);
  D_Flip_Flop d_ff_1 (.D(or_1_out), .clk(button_1_out), .Q(d_ff_1_q));  // open: Qn, preset, reset
  D_Flip_Flop d_ff_2 (.D(or_2_out), .clk(button_1_out), .Q(d_ff_2_q));  // open: Qn, preset, reset
  D_Flip_Flop d_ff_3 (.D(or_3_out), .clk(button_1_out), .Q(d_ff_3_q));  // open: Qn, preset, reset
  Button button_1 (.out(button_1_out));
  D_Flip_Flop d_ff_4 (.D(or_4_out), .clk(button_1_out), .Q(d_ff_4_q));  // open: Qn, preset, reset
  // Probe on d_ff_1_q
  // Probe on d_ff_2_q
  // Probe on d_ff_3_q
  // Probe on d_ff_4_q
endmodule
