// Logisim project shiftRegisterSpecialNum.circ as structural Verilog: 1 circuit, main circuit main
module main (
  input  in_1,
  input  in_2,
  input  in_3,
  input  in_4,
  input  in_5,
  input  in_6,
  output QA,
  output QB,
  output out_9,
  output QC,
  output QD
);

  wire button_1_out, not_1_out, xnor_1_out, xor_1_out;

  Button button_1 (.out(button_1_out));
  not not_1 (not_1_out, in_1);
  // Shift_Register #(.length(4)) shift_register_1: pin names not known; wires that end beside it: in_1, not_1_out, button_1_out, in_2, in_3, in_4, in_5, in_6, QA, QB, QC, QD
  xnor xnor_1 (xnor_1_out, QB, QA);
  xor xor_1 (xor_1_out, QD, QC);
  and and_1 (out_9, xnor_1_out, xor_1_out);
endmodule
